# Fritzing sketch abreuvoir_connecte (saved by Fritzing 0.9.3b)

parts:
  Composant1 = Arduino Nano (Rev3.0) (ICSP)
  C1 = Capacitor Polarized [package=panasonic_g]
  Squix1 = OLED 0.96" 128x64 I2C SSD1306
  J10 = Camdenboss CTB0158-2 [part_number=CTB0158-2 package=THT]
  U1 = Voltage Regulator - 5V [package="DPak [SMD]"]
  C2 = Electrolytic Capacitor [capacitance=10μF package="0605 [SMD, electrolytic]"]
  Q4 = TIP120 Hi-Current Darlington Transistor
  R4 = Resistor [tolerance=±5% resistance=2.2k package="0603 [SMD]"]
  J11 = Camdenboss CTB0158-2 [part_number=CTB0158-2 package=THT]
  D4 = Rectifier Diode [part_number=1N4001 package="300 mil [THT]"]
  Q5 = TIP120 Hi-Current Darlington Transistor
  J12 = Camdenboss CTB0158-2 [part_number=CTB0158-2 package=THT]
  R5 = Resistor [tolerance=±5% resistance=2.2k package="0603 [SMD]"]
  D5 = Rectifier Diode [part_number=1N4001 package="300 mil [THT]"]
  Q6 = TIP120 Hi-Current Darlington Transistor
  J13 = Camdenboss CTB0158-2 [part_number=CTB0158-2 package=THT]
  R6 = Resistor [tolerance=±5% resistance=2.2k package="0603 [SMD]"]
  D6 = Rectifier Diode [part_number=1N4001 package="300 mil [THT]"]
  J14 = female pin header, 3 pins [form="♀ (female)"]
  J15 = female pin header, 3 pins [form="♀ (female)"]
  J16 = female pin header, 3 pins [form="♀ (female)"]
  J17 = female pin header, 4 pins [form="♀ (female)"]
  J18 = female pin header, 4 pins [form="♀ (female)"]

nets:
  GND: Composant1.GND, Squix1.GND, J14.pin1, J15.pin1, J16.pin1, J17.pin1, J18.pin1
  N1: Composant1.D4, R4.Pin_1
  N2: Composant1.D5, R5.Pin_1
  N3: Composant1.D6, R6.Pin_1
  N4: Composant1.D8, J18.pin3
  N5: Composant1.D9, J18.pin4
  N6: Composant1.5V, U1.output_voltage, C2.+, J14.pin3, J15.pin3, J16.pin3, J17.pin4, J18.pin2
  N7: Composant1.A5, Squix1.SCL
  N8: Composant1.A4, Squix1.SCA
  N9: Composant1.A2, J17.pin2
  N10: Composant1.A1, J17.pin3
  3V3: Composant1.3V3, Squix1.VCC
  N11: C1.+, J10.pin2, U1.input_voltage, J11.pin1, D4.cathode, J12.pin1, D5.cathode, J13.pin1, D6.cathode
  N12: C1.-, J10.pin1, U1.GND, C2.-, Q4.EMITTER, Q5.EMITTER, Q6.EMITTER
  N13: Q4.BASE, R4.Pin_0
  N14: Q4.COLLECTOR, J11.pin2, D4.anode
  N15: Q5.BASE, R5.Pin_0
  N16: Q5.COLLECTOR, J12.pin2, D5.anode
  N17: Q6.BASE, R6.Pin_0
  N18: Q6.COLLECTOR, J13.pin2, D6.anode

notes:
  ---(LTR)--->
  RFID reader,
  Range sensor,
  Pressure sensor,
  Flow IN,
  Flow OUT
  12V battery
  Valve IN Pump Valve OUT
  [ - +] [ - +] [ - +]
  [optionnal]
  SD logger & RTC integrated in shield
